// Logisim project Arithmetic Logic Unit.circ as structural Verilog
module main (
  input  in_1,
  input  in_2,
  input  [2:0] in_3,
  input  in_4,
  output out_5,
  output out_6
);

  wire clock_1_out, control_unit_1_and_ld, control_unit_1_dr_ld, control_unit_1_out_3, control_unit_1_out_4,
       control_unit_1_out_8, control_unit_1_out_9, control_unit_1_out_10, control_unit_1_out_11,
       control_unit_1_out_15, control_unit_1_read, control_unit_1_sub_ld, control_unit_1_write;
  wire [2:0] control_unit_1_out_14;
  wire [5:0] AR_q, bit_extender_1_out;
  wire [15:0] AC_q, alu_1_alu_output, bit_extender_2_out, DR_q, IR_q, multiplexer_1_out, PC_q, ram_1_data,
       TR_q;

  Clock clock_1 (.out(clock_1_out));
  Control_Unit control_unit_1 (
    .IR(IR_q), .out_3(control_unit_1_out_3), .READ(control_unit_1_read), .DR_LD(control_unit_1_dr_ld),
    .WRITE(control_unit_1_write), .out_8(control_unit_1_out_8), .out_9(control_unit_1_out_9),
    .out_11(control_unit_1_out_11), .AND_LD(control_unit_1_and_ld), .SUB_LD(control_unit_1_sub_ld),
    .out_10(control_unit_1_out_10), .out_14(control_unit_1_out_14), .in_2(clock_1_out),
    .out_15(control_unit_1_out_15), .out_4(control_unit_1_out_4));
  Bit_Extender #(.in_width(16), .out_width(6)) bit_extender_1 (.in(multiplexer_1_out), .out(bit_extender_1_out));
  Register #(.width(16)) AC (
    .D(alu_1_alu_output), .en(control_unit_1_out_3), .Q(AC_q), .clk(clock_1_out));  // open: clr
  Register #(.width(16)) DR (
    .D(multiplexer_1_out), .en(control_unit_1_dr_ld), .Q(DR_q), .clk(clock_1_out));  // open: clr
  Register #(.width(6)) AR (
    .D(bit_extender_1_out), .en(control_unit_1_out_15), .Q(AR_q), .clk(clock_1_out));  // open: clr
  Register #(.width(16)) TR (.D(multiplexer_1_out), .en(in_4), .Q(TR_q), .clk(clock_1_out));  // open: clr
  Counter #(.width(16), .max('hffff), .ongoal("continue")) PC (
    .load(control_unit_1_out_8), .D(multiplexer_1_out), .count(control_unit_1_out_9), .Q(PC_q),
    .clk(clock_1_out));  // open: carry, clr
  Register #(.width(16)) IR (
    .D(multiplexer_1_out), .en(control_unit_1_out_4), .Q(IR_q), .clk(clock_1_out));  // open: clr
  RAM #(.addrWidth(6), .dataWidth(16), .bus("separate")) ram_1 (
    .addr(AR_q), .din(multiplexer_1_out), .data(ram_1_data), .str(control_unit_1_write), .clk(clock_1_out),
    .ld(control_unit_1_read));  // open: sel, clr
  ALU alu_1 (
    .in_1(in_1), .Input_1__AC(AC_q), .Input_2__DR(DR_q), .in_4(in_2), .Selection_of_ALU(in_3),
    .out_10(out_5), .out_11(out_6), .ALU_Output(alu_1_alu_output), .in_8(control_unit_1_and_ld),
    .in_9(control_unit_1_out_11), .in_7(control_unit_1_out_10), .in_6(control_unit_1_sub_ld));
  assign bit_extender_2_out = {{10{1'b0}}, AR_q};  // Bit_Extender bit_extender_2
  Multiplexer #(.select(3), .width(16)) multiplexer_1 (
    .in0(AC_q), .in1(DR_q), .in2(TR_q), .in3(bit_extender_2_out), .in4(ram_1_data), .in5(PC_q), .in6(IR_q),
    .out(multiplexer_1_out), .sel(control_unit_1_out_14));  // open: in7, en
endmodule

module ALU (
  input  in_1,
  input  [15:0] Input_1__AC,
  input  [15:0] Input_2__DR,
  input  in_4,
  input  [2:0] Selection_of_ALU,
  input  in_6,
  input  in_7,
  input  in_8,
  input  in_9,
  output out_10,
  output out_11,
  output [15:0] ALU_Output
);

  wire [15:0] adder_1_out, and_1_out, Complement_AC__DR_is_also_correct_out, controlled_buffer_1_out,
       controlled_buffer_2_out, controlled_buffer_3_out, controlled_buffer_4_out, or_1_out, subtractor_1_out,
       xor_1_out;

  Adder #(.width(16)) adder_1 (.a(Input_1__AC), .b(Input_2__DR), .out(adder_1_out), .cin(in_1), .cout(out_10));
  Subtractor #(.width(16)) subtractor_1 (
    .a(Input_1__AC), .b(Input_2__DR), .out(subtractor_1_out), .bin(in_4), .bout(out_11));
  assign controlled_buffer_1_out = in_7 ? Input_2__DR : 16'bz;  // Controlled_Buffer controlled_buffer_1
  assign and_1_out = Input_1__AC & Input_2__DR;  // AND_Gate and_1, 16 bits wide
  assign or_1_out = Input_1__AC | Input_2__DR;  // OR_Gate or_1, 16 bits wide
  assign xor_1_out = Input_1__AC ^ Input_2__DR;  // XOR_Gate xor_1, 16 bits wide
  assign Complement_AC__DR_is_also_correct_out = ~Input_1__AC;  // NOT_Gate Complement_AC__DR_is_also_correct, 16 bits wide
  assign controlled_buffer_2_out = in_6 ? subtractor_1_out : 16'bz;  // Controlled_Buffer controlled_buffer_2
  Multiplexer #(.select(3), .width(16)) multiplexer_1 (
    .in0(adder_1_out), .in1(controlled_buffer_2_out), .in2(controlled_buffer_1_out),
    .in3(controlled_buffer_3_out), .in4(controlled_buffer_4_out), .in5(xor_1_out),
    .in6(Complement_AC__DR_is_also_correct_out), .out(ALU_Output), .sel(Selection_of_ALU));  // open: in7, en
  assign controlled_buffer_3_out = in_8 ? and_1_out : 16'bz;  // Controlled_Buffer controlled_buffer_3
  assign controlled_buffer_4_out = in_9 ? or_1_out : 16'bz;  // Controlled_Buffer controlled_buffer_4
endmodule

module Control_Unit (
  input  [15:0] IR,
  input  in_2,
  output out_3,
  output out_4,
  output READ,
  output DR_LD,
  output WRITE,
  output out_8,
  output out_9,
  output out_10,
  output out_11,
  output AND_LD,
  output SUB_LD,
  output [2:0] out_14,
  output out_15
);

  wire and_1_out, and_2_out, and_3_out, and_4_out, and_5_out, and_6_out, and_7_out, and_8_out, and_9_out,
       and_10_out, and_11_out, and_12_out, and_13_out, and_14_out, and_15_out, and_16_out, and_17_out,
       and_18_out, and_19_out, and_20_out, and_21_out, and_22_out, and_23_out, d_ff_1_q, decoder_1_out0,
       decoder_1_out1, decoder_1_out2, decoder_1_out3, decoder_1_out4, decoder_1_out5, decoder_1_out6,
       decoder_1_out7, decoder_2_out0, decoder_2_out2, decoder_2_out3, decoder_2_out4, decoder_2_out5,
       decoder_2_out6, decoder_2_out7, decoder_2_out8, decoder_2_out9, decoder_2_out10, decoder_2_out11,
       decoder_2_out12, decoder_2_out13, decoder_2_out14, not_1_out, or_1_out, or_2_out, SC_Clear_out;
  wire [3:0] counter_1_q;

  Counter #(.width(4), .max('hf), .ongoal("stay")) counter_1 (
    .Q(counter_1_q), .clk(in_2), .clr(d_ff_1_q));  // open: load, D, count, carry
  D_Flip_Flop d_ff_1 (.clk(in_2), .D(SC_Clear_out), .Q(d_ff_1_q));  // open: Qn, preset, en, reset
  and and_1 (and_1_out, decoder_1_out1, decoder_2_out4);
  and and_2 (and_2_out, decoder_1_out2, decoder_2_out4);
  and and_3 (and_3_out, decoder_1_out0, decoder_2_out4);
  and and_4 (and_4_out, decoder_1_out5, decoder_2_out4);
  Decoder #(.select(3)) decoder_1 (
    .out0(decoder_1_out0), .out1(decoder_1_out1), .out2(decoder_1_out2), .out3(decoder_1_out3),
    .out4(decoder_1_out4), .out5(decoder_1_out5), .out6(decoder_1_out6), .out7(decoder_1_out7),
    .sel(IR[14:12]));  // open: en
  Decoder #(.select(4)) decoder_2 (
    .out0(decoder_2_out0), .out1(out_4), .out2(decoder_2_out2), .out3(decoder_2_out3), .out4(decoder_2_out4),
    .out5(decoder_2_out5), .out6(decoder_2_out6), .out7(decoder_2_out7), .out8(decoder_2_out8),
    .out9(decoder_2_out9), .out10(decoder_2_out10), .out11(decoder_2_out11), .out12(decoder_2_out12),
    .out13(decoder_2_out13), .out14(decoder_2_out14), .sel(counter_1_q));  // open: out15, en
  or or_1 (or_1_out, and_1_out, and_2_out, out_4, and_3_out, and_4_out);
  or or_2 (or_2_out, decoder_2_out6, decoder_2_out7, decoder_2_out8, decoder_2_out9, decoder_2_out10, decoder_2_out11, decoder_2_out12, decoder_2_out13, decoder_2_out14);
  and and_5 (and_5_out, decoder_2_out4, decoder_1_out4);
  and and_6 (and_6_out, decoder_1_out3, decoder_2_out4);
  Priority_Encoder priority_encoder_1 (
    .in0(and_6_out), .in3(and_5_out), .in4(or_1_out), .in5(decoder_2_out0), .in6(decoder_2_out2),
    .out(out_14), .en_in(1'b1));  // open: in1, in2, in7, gs, en_out
  and and_7 (and_7_out, decoder_1_out2, decoder_2_out5);
  and and_8 (and_8_out, decoder_1_out1, decoder_2_out5);
  and and_9 (and_9_out, decoder_1_out0, decoder_2_out5);
  and and_10 (and_10_out, decoder_1_out2, decoder_2_out4);
  and and_11 (and_11_out, decoder_1_out1, decoder_2_out4);
  and and_12 (and_12_out, decoder_1_out5, decoder_2_out4);
  and and_13 (and_13_out, decoder_2_out4, decoder_1_out0);
  and and_14 (and_14_out, decoder_1_out2, decoder_2_out4);
  and and_15 (and_15_out, decoder_1_out1, decoder_2_out4);
  and and_16 (and_16_out, decoder_1_out5, decoder_2_out4);
  and and_17 (and_17_out, decoder_1_out0, decoder_2_out4);
  and and_18 (and_18_out, decoder_1_out2, decoder_2_out5);
  and and_19 (and_19_out, decoder_1_out1, decoder_2_out5);
  and and_20 (and_20_out, decoder_1_out5, decoder_2_out5);
  and and_21 (and_21_out, decoder_1_out4, decoder_2_out4);
  and and_22 (and_22_out, decoder_1_out0, decoder_2_out5);
  and and_23 (and_23_out, decoder_1_out3, decoder_2_out4);
  or or_3 (out_15, decoder_2_out0, decoder_2_out2);
  or or_4 (out_3, and_7_out, and_9_out, and_8_out);
  or or_5 (READ, out_4, and_10_out, and_11_out, and_12_out, and_13_out);
  or or_6 (DR_LD, and_14_out, and_15_out, and_16_out, and_17_out);
  and and_24 (WRITE, decoder_1_out3, decoder_2_out4);
  and and_25 (out_8, decoder_1_out4, decoder_2_out4);
  not not_1 (not_1_out, IR[15]);
  and and_26 (out_9, not_1_out, decoder_1_out7, decoder_2_out3, IR[2]);
  and and_27 (out_10, decoder_1_out2, decoder_2_out5);
  and and_28 (out_11, decoder_1_out1, decoder_2_out5);
  and and_29 (AND_LD, decoder_1_out0, decoder_2_out5);
  or SC_Clear (SC_Clear_out, and_18_out, and_19_out, and_20_out, and_21_out, and_22_out, and_23_out);
  and and_30 (SUB_LD, decoder_1_out5, decoder_2_out5);
  // also tied to GND on the sheet: {or_2_out, decoder_1_out6}

  // Notes on the sheet:
  //   T3
  //   D7
  //   D0
  //   D1
  //   D2
  //   D3
  //   D4
  //   D5
  //   D6
  //   T2
  //   T6
  //   T0
  //   T1
  //   T4
  //   T5
  //   AC LD
  //   PC LD
  //   PC INC
  //   TNS LD
  //   ADD LD
endmodule
